// Digital circuit pong.dig as structural Verilog
module pong (
  input  Master_VGA_Clock,
  input  in_2,
  input  Test_Clock,
  input  in_4,
  input  in_5,
  input  Manual_Clock
);

  wire _74163_1_pin15, _74163_2_pin15, _74163_4_pin15, _74163_5_pin15, and_1_out, and_2_out, CLK, H0, H1, H2,
       H3, H4, H5, H6, H7, H8, H9, H10, H11, HCLR, HSYNC, not_1_out, not_2_out, not_3_out, not_4_out,
       not_5_out, not_6_out, not_7_out, not_8_out, not_9_out, not_10_out, V0, V1, V2, V3, V4, V5, V6, V7, V8,
       V9, V10, V11, VCLR, VSYNC;

  // Relay relay_1: pin names not known; wires that end beside it: Master_VGA_Clock, CLK
  // Relay relay_2: pin names not known; wires that end beside it: in_2, Test_Clock, in_4, in_5, 1'b0, CLK, 1'b0, 1'b0
  // Relay relay_3: pin names not known; wires that end beside it: Manual_Clock, CLK
  _74163 _74163_1 (
    .pin1(HCLR), .pin2(CLK), .pin3(1'b0), .pin4(1'b0), .pin5(1'b0), .pin6(1'b0), .pin7(1'b1), .pin8(1'b0),
    .pin9(1'b1), .pin10(1'b1), .pin11(H3), .pin12(H2), .pin13(H1), .pin14(H0), .pin15(_74163_1_pin15),
    .pin16(1'b1));
  _74163 _74163_2 (
    .pin1(HCLR), .pin2(CLK), .pin3(1'b0), .pin4(1'b0), .pin5(1'b0), .pin6(1'b0), .pin7(1'b1), .pin8(1'b0),
    .pin9(1'b1), .pin10(_74163_1_pin15), .pin11(H7), .pin12(H6), .pin13(H5), .pin14(H4),
    .pin15(_74163_2_pin15), .pin16(1'b1));
  _74163 _74163_3 (
    .pin1(HCLR), .pin2(CLK), .pin3(1'b0), .pin4(1'b0), .pin5(1'b0), .pin6(1'b0), .pin7(1'b1), .pin8(1'b0),
    .pin9(1'b1), .pin10(_74163_2_pin15), .pin11(H11), .pin12(H10), .pin13(H9), .pin14(H8), .pin16(1'b1));  // open: pin15
  // Probe on {H9, H8, H7, H6, H5, H4, H3, H2, H1, H0}
  LED led_1 (.in(H9));
  LED led_2 (.in(H8));
  LED led_3 (.in(V9));
  LED led_4 (.in(V8));
  Comparator #(.Bits(10)) comparator_1 (.a({H9, H8, H7, H6, H5, H4, H3, H2, H1, H0}));  // open: b, gt, eq, lt
  LED led_5 (.in(H7));
  LED led_6 (.in(H6));
  LED led_7 (.in(V7));
  LED led_8 (.in(V6));
  LED led_9 (.in(H5));
  LED led_10 (.in(H4));
  LED led_11 (.in(V5));
  LED led_12 (.in(V4));
  LED led_13 (.in(H3));
  LED led_14 (.in(H2));
  LED led_15 (.in(V3));
  LED led_16 (.in(V2));
  // Probe on {V9, V8, V7, V6, V5, V4, V3, V2, V1, V0}
  _74163 _74163_4 (
    .pin1(VCLR), .pin2(HCLR), .pin3(1'b0), .pin4(1'b0), .pin5(1'b0), .pin6(1'b0), .pin7(1'b1), .pin8(1'b0),
    .pin9(1'b1), .pin10(1'b1), .pin11(V3), .pin12(V2), .pin13(V1), .pin14(V0), .pin15(_74163_4_pin15),
    .pin16(1'b1));
  _74163 _74163_5 (
    .pin1(VCLR), .pin2(HCLR), .pin3(1'b0), .pin4(1'b0), .pin5(1'b0), .pin6(1'b0), .pin7(1'b1), .pin8(1'b0),
    .pin9(1'b1), .pin10(_74163_4_pin15), .pin11(V7), .pin12(V6), .pin13(V5), .pin14(V4),
    .pin15(_74163_5_pin15), .pin16(1'b1));
  _74163 _74163_6 (
    .pin1(VCLR), .pin2(HCLR), .pin3(1'b0), .pin4(1'b0), .pin5(1'b0), .pin6(1'b0), .pin7(1'b1), .pin8(1'b0),
    .pin9(1'b1), .pin10(_74163_5_pin15), .pin11(V11), .pin12(V10), .pin13(V9), .pin14(V8), .pin16(1'b1));  // open: pin15
  LED led_17 (.in(H1));
  LED led_18 (.in(H0));
  LED led_19 (.in(V1));
  LED led_20 (.in(V0));
  and and_1 (and_1_out, H9, H8, not_1_out, not_2_out, not_3_out, H4, H3, H2, H1, H0);
  not not_1 (not_1_out, H7);
  not not_2 (not_2_out, H6);
  not not_3 (not_3_out, H5);
  and and_2 (and_2_out, V9, not_4_out, not_5_out, not_6_out, not_7_out, not_8_out, V3, V2, not_9_out, not_10_out);
  not not_4 (not_4_out, V8);
  not not_5 (not_5_out, V7);
  not not_6 (not_6_out, V6);
  not not_7 (not_7_out, V5);
  not not_8 (not_8_out, V4);
  not not_9 (not_9_out, V1);
  not not_10 (not_10_out, V0);
  not not_11 (HCLR, and_1_out);
  not not_12 (VCLR, and_2_out);
  VGA vga_1 (.R(1'b1), .G(1'b1), .B(1'b1), .H(HSYNC), .V(VSYNC), .C(CLK));

  // Other names for the same wires on the sheet: HCOUNT[9:0] = {H9, H8, H7, H6, H5, H4, H3, H2, H1, H0};
  //   VCOUNT[9:0] = {V9, V8, V7, V6, V5, V4, V3, V2, V1, V0}

  // Notes on the sheet:
  //   Master_VGA_Clock: Hz: 25175000
  //   Test_Clock: Hz: 1000
endmodule
